# Fritzing sketch esp8266-led-rgb (saved by Fritzing 0.9.3b)
breadboards: 1

parts:
  U2 = NodeMCU V3.0
  LED1 = RGB LED (com. anode, rbg) [package="5 mm [THT]"]
  R1 = Resistor [tolerance=±5% resistance=220 package="0603 [SMD]"]
  R2 = Resistor [tolerance=±5% resistance=220 package="0603 [SMD]"]
  R3 = Resistor [tolerance=±5% resistance=220 package="0603 [SMD]"]

nets:
  N1: U2.3V3, LED1.common_anode
  N2: U2.GND#6, U2.GND#13, U2.GND#16, U2.GND#33
  N3: U2.D5, R1.Pin_1
  N4: U2.D6, R2.Pin_1
  N5: U2.D7, R3.Pin_1
  N6: LED1.red_cathode, R1.Pin_0
  N7: LED1.blue_cathode, R2.Pin_0
  N8: LED1.green_cathode, R3.Pin_0

custom parts:
  NodeMCU V3.0: ESP8266 based NodeMCU
